# Fritzing sketch 08-Pulsador_led_PLC (saved by Fritzing 0.9.3b)
breadboards: 1

parts:
  Parte1 = Arduino Uno (Rev3)
  ON/OFF = Pushbutton [package="[THT]"]
  R5 = Resistor [tolerance=±5% resistance=10k package="0805 [SMD]"]
  LED1 = LED - 5mm [color="Green (555nm)" package="5 mm [THT]"]
  R6 = Resistor [tolerance=±5% resistance=220 package="0805 [SMD]"]

nets:
  N1: Parte1.A5/SCL, Parte1.D8, ON/OFF.Pin_1, ON/OFF.Pin_2, R5.Pin_0
  N2: Parte1.D11_PWM/MOSI, LED1.anode
  N3: Parte1.5V, ON/OFF.Pin_3, ON/OFF.Pin_4
  N4: Parte1.GND, R6.Pin_1
  N5: LED1.cathode, R6.Pin_0
