# Fritzing sketch 16-disparo-alarma (saved by Fritzing 0.9.3b)
breadboards: 1

parts:
  Parte1 = Arduino Uno (Rev3)
  SET = Pushbutton [package="[THT]"]
  R5 = Resistor [tolerance=±5% resistance=10k package="0805 [SMD]"]
  J1 = Piezo Speaker

nets:
  N1: Parte1.A1, SET.Pin_1, SET.Pin_2, R5.Pin_0
  N2: Parte1.D3_PWM, J1.pin2
  N3: Parte1.5V, SET.Pin_3, SET.Pin_4
  N4: Parte1.GND, J1.pin1
