# Fritzing sketch DIY Arduino Traffic Light Pedestrian Light Push Button Control (saved by Fritzing 0.9.2b)
breadboards: 1

parts:
  Part1 = Arduino Uno (Rev3)
  LED1 = LED - 5mm [color="Green (555nm)" package="5 mm [THT]"]
  LED2 = LED - 5mm [color="Yellow (595nm)" package="5 mm [THT]"]
  LED3 = LED - 5mm [color="Red (633nm)" package="5 mm [THT]"]
  LED4 = LED - 5mm [color="Red (633nm)" package="5 mm [THT]"]
  LED5 = LED - 5mm [color="Green (555nm)" package="5 mm [THT]"]
  R1 = Resistor [tolerance=±5% resistance=1k package=THT]
  R2 = Resistor [tolerance=±5% resistance=1k package=THT]
  R3 = Resistor [tolerance=±5% resistance=1k package=THT]
  R4 = Resistor [tolerance=±5% resistance=1k package=THT]
  R5 = Resistor [tolerance=±5% resistance=1k package=THT]
  S1 = Pushbutton [package="[THT]"]
  R6 = Resistor [tolerance=±5% resistance=1M package=THT]

nets:
  N1: Part1.D8, R4.Pin_1
  N2: Part1.D9_PWM, R5.Pin_1
  N3: LED1.cathode, LED2.cathode, LED3.cathode, LED4.cathode, LED5.cathode, R6.Pin_0
  N4: LED1.anode, R3.Pin_0
  N5: LED2.anode, R2.Pin_0
  N6: LED3.anode, R1.Pin_0
  N7: LED4.anode, R4.Pin_0
  N8: LED5.anode, R5.Pin_0
  N9: S1.Pin_1, S1.Pin_2
  N10: S1.Pin_3, S1.Pin_4, R6.Pin_1

// code stored in the sketch: DIY Arduino Traffic Light Pedestrian Light Push Button Control.ino
int TrafficRed = 3;  
int TrafficYellow = 4;
int TrafficGreen = 5;
int PedestrianRed = 8;  
int PedestrianGreen = 9;
int button = 13; 
int crossTime = 4000;   
unsigned long buttonGap ; 
void setup () {
  pinMode(TrafficRed, OUTPUT);
  pinMode(TrafficYellow, OUTPUT);
  pinMode(TrafficGreen, OUTPUT);
  pinMode(PedestrianRed, OUTPUT);
  pinMode(PedestrianGreen, OUTPUT);
  pinMode(button, INPUT);
 
  digitalWrite(TrafficGreen,HIGH); 
  digitalWrite(PedestrianRed, HIGH);
}

void loop(){
  int state = digitalRead(button);
  if(state==HIGH && (millis() - buttonGap) > 5000) {
    switchLights();   
  }
}

void switchLights() {
  digitalWrite(TrafficGreen,LOW); 
  digitalWrite(TrafficYellow,HIGH); 
  delay(2000);

  digitalWrite(TrafficYellow,LOW);
  digitalWrite(TrafficRed,HIGH); 
  delay(1000);

  digitalWrite(PedestrianRed,LOW); 
  digitalWrite(PedestrianGreen,HIGH); 
  delay(crossTime);

  for (int x=0; x<10; x++){
    digitalWrite(PedestrianGreen,HIGH);
    delay(250);
    digitalWrite(PedestrianGreen,LOW);
    delay(250);
  }
 
  digitalWrite(PedestrianRed, HIGH); 
  delay(100);
 
  digitalWrite(TrafficRoadGreen,HIGH);
  digitalWrite(TrafficRoadRed,LOW);
 
  buttonGap = millis(); 
 
}
