# Fritzing sketch PROYECTO-CURSO-Cruce_Controlado (saved by Fritzing 0.9.3b)
breadboards: 1

parts:
  Parte1 = Arduino Uno (Rev3)
  part = Resistor [tolerance=±5% resistance=10k package="0805 [SMD]"]
  LED2 = LED - 5mm [color="Red (633nm)" package="5 mm [THT]"]
  LED3 = LED - 5mm [color="Red (633nm)" package="5 mm [THT]"]
  LED4 = LED - 5mm [color="Green (555nm)" package="5 mm [THT]"]
  LED5 = LED - 5mm [color="Green (555nm)" package="5 mm [THT]"]
  R7 = Resistor [tolerance=±5% resistance=220 package="0805 [SMD]"]
  part_2 = Resistor [tolerance=±5% resistance=220 package="0805 [SMD]"]
  R9 = Resistor [tolerance=±5% resistance=220 package="0805 [SMD]"]
  R10 = Resistor [tolerance=±5% resistance=220 package="0805 [SMD]"]
  ON/OFF = Pushbutton [package="[THT]"]

nets:
  N1: Parte1.A1, part.Pin_0, ON/OFF.Pin_1, ON/OFF.Pin_2
  N2: Parte1.D3_PWM, LED5.anode
  N3: Parte1.D5_PWM, LED2.anode
  N4: Parte1.D6_PWM, LED4.anode
  N5: Parte1.5V, ON/OFF.Pin_3, ON/OFF.Pin_4
  N6: Parte1.GND, part.Pin_1, R7.Pin_1, part_2.Pin_1, R9.Pin_1, R10.Pin_1
  N7: LED2.cathode, R9.Pin_0
  N8: LED3.anode, R7.Pin_0
  N9: LED4.cathode, part_2.Pin_0
  N10: LED5.cathode, R10.Pin_0
