# Fritzing sketch PROYECTO-CURSO-Cruce_Controlado_peaton (saved by Fritzing 0.9.3b)
breadboards: 1

parts:
  Parte1 = Arduino Uno (Rev3)
  R5 = Resistor [tolerance=±5% resistance=10k package="0805 [SMD]"]
  LED1 = LED - 5mm [color="Blue (430nm)" package="5 mm [THT]"]
  R6 = Resistor [tolerance=±5% resistance=220 package="0805 [SMD]"]
  LED2 = LED - 5mm [color="Red (633nm)" package="5 mm [THT]"]
  LED3 = LED - 5mm [color="Red (633nm)" package="5 mm [THT]"]
  LED4 = LED - 5mm [color="Green (555nm)" package="5 mm [THT]"]
  LED5 = LED - 5mm [color="Green (555nm)" package="5 mm [THT]"]
  R7 = Resistor [tolerance=±5% resistance=220 package="0805 [SMD]"]
  R8 = Resistor [tolerance=±5% resistance=220 package="0805 [SMD]"]
  R9 = Resistor [tolerance=±5% resistance=220 package="0805 [SMD]"]
  R10 = Resistor [tolerance=±5% resistance=220 package="0805 [SMD]"]
  part = Pushbutton [package="[THT]"]

nets:
  N1: Parte1.A1, R5.Pin_0, part.Pin_1, part.Pin_2
  N2: Parte1.D3_PWM, LED5.anode
  N3: Parte1.D5_PWM, LED1.anode, LED2.anode
  N4: Parte1.D6_PWM, LED4.anode
  N5: Parte1.5V, part.Pin_3, part.Pin_4
  N6: Parte1.GND, R5.Pin_1, R6.Pin_1, R7.Pin_1, R8.Pin_1, R9.Pin_1, R10.Pin_1
  N7: LED1.cathode, R6.Pin_0
  N8: LED2.cathode, R9.Pin_0
  N9: LED3.anode, R7.Pin_0
  N10: LED4.cathode, R8.Pin_0
  N11: LED5.cathode, R10.Pin_0
